# Fritzing sketch pcb (saved by Fritzing 0.9.3b)
circuit board: 8.77182cm x 5.3106cm

parts:
  1ok = Resistor [tolerance=±5% resistance=220 package=THT]
  10k = Resistor [tolerance=±5% resistance=220 package="2512 [SMD]"]
  68ohm = Resistor [tolerance=±5% resistance=220 package=THT]
  APSwitch = Round Pushbutton
  TP4056 = TP4056 [chip_label=TP4056 package="DIP (Dual Inline) [THT]"]
  I2C = CNZ1120 [package=cnz1120]
  PhotoInterrupter = CNZ1120 [package=cnz1120]
  ESP8266_CP2102 = NodeMCU V1.0
  buzzer = Piezo Speaker - PC Mount [part_number=COM-07950]

nets (from the pcb view):
  N1: 1ok.Pin_0, 10k.Pin_1, I2C.E, ESP8266_CP2102.3V3
  N2: 1ok.Pin_1, PhotoInterrupter.+#3
  N3: 10k.Pin_0, PhotoInterrupter.+#1
  N4: 68ohm.Pin_0, ESP8266_CP2102.A0
  N5: 68ohm.Pin_1, PhotoInterrupter.D
  N6: APSwitch.leg0, ESP8266_CP2102.D4
  GND: APSwitch.leg1, TP4056.pin6, I2C.+#1, PhotoInterrupter.E, ESP8266_CP2102.GND, buzzer.GND
  N7: TP4056.pin3, ESP8266_CP2102.Vin
  N8: I2C.D, ESP8266_CP2102.D1
  N9: I2C.+#3, ESP8266_CP2102.D2
  N10: ESP8266_CP2102.D8, buzzer.VCC

custom parts:
  TP4056: A DIP stand-in part for whatever IC you want. With 6 pins on a 300mil dual inline package (DIP) footprint.
  CNZ1120: LED-to-NPN optoisolator
  NodeMCU V1.0: ESP8266 based NodeMCU
  Piezo Speaker - PC Mount: This is a small 12mm round speaker that operates around the audible 2kHz range. You can use these speakers to create simple music or user interfaces. Each speaker is PTH solderable and requires an operating voltage of 3.5-5V with a mean current of 35mA max. These speakers also have a typical sound output of 95 dBA and a coil resistance of 42 ±6.3 ohms.
